// Logisim project ex1.circ as structural Verilog: 1 circuit, main circuit main
module main (
  input  A,
  input  B,
  output AND,
  output OR
);

  wire and_1_out, not_1_out, not_2_out, not_3_out, not_4_out, or_1_out;

  not not_1 (not_1_out, A);
  not not_2 (not_2_out, B);
  not not_3 (not_3_out, A);
  not not_4 (not_4_out, B);
  or or_1 (or_1_out, not_1_out, not_2_out);
  not not_5 (AND, or_1_out);
  not not_6 (OR, and_1_out);
  and and_1 (and_1_out, not_3_out, not_4_out);

  // Notes on the sheet:
  //   EXERCICIO 1
endmodule
