// Logisim project ex3.circ as structural Verilog: 1 circuit, main circuit main
module main (
  input  A,
  input  B,
  input  C,
  output S,
  output T
);

  wire nand_1_out, nand_2_out, nand_3_out, nand_4_out, nand_5_out, nand_6_out, nand_7_out, nand_8_out,
       nand_9_out, nand_10_out, nand_11_out, nand_12_out, nand_13_out, nand_15_out, nand_16_out, nand_17_out,
       nand_18_out, nand_19_out, nand_20_out, nand_21_out, nand_22_out, nand_23_out;

  nand nand_1 (nand_1_out, A, B);
  nand nand_2 (nand_2_out, A, C);
  nand nand_3 (nand_3_out, B, C);
  nand nand_4 (nand_4_out, A, B);
  not nand_5 (nand_5_out, A);  // NAND_Gate
  not nand_6 (nand_6_out, B);  // NAND_Gate
  nand nand_7 (nand_7_out, A, C);
  not nand_8 (nand_8_out, A);  // NAND_Gate
  not nand_9 (nand_9_out, C);  // NAND_Gate
  nand nand_10 (nand_10_out, B, C);
  not nand_11 (nand_11_out, B);  // NAND_Gate
  not nand_12 (nand_12_out, C);  // NAND_Gate
  nand nand_13 (nand_13_out, A, B, B, C);
  nand nand_14 (S, nand_1_out, nand_2_out, nand_3_out);
  nand nand_15 (nand_15_out, nand_4_out, nand_5_out, nand_6_out);
  nand nand_16 (nand_16_out, nand_7_out, nand_8_out, nand_9_out);
  nand nand_17 (nand_17_out, nand_10_out, nand_11_out, nand_12_out);
  not nand_18 (nand_18_out, nand_15_out);  // NAND_Gate
  not nand_19 (nand_19_out, nand_16_out);  // NAND_Gate
  not nand_20 (nand_20_out, nand_17_out);  // NAND_Gate
  nand nand_21 (nand_21_out, nand_18_out, C);
  nand nand_22 (nand_22_out, nand_19_out, B);
  nand nand_23 (nand_23_out, nand_20_out, A);
  nand nand_24 (T, nand_21_out, nand_22_out, nand_23_out, nand_13_out);
endmodule
