// Logisim project ex4.circ as structural Verilog: 1 circuit, main circuit main
module main (
  input  D0,
  input  D1,
  input  D2,
  input  D3,
  input  S1,
  input  S0,
  output Y
);

  wire nand_1_out, nand_2_out, nand_3_out, nand_4_out, nand_5_out, nand_6_out, nand_7_out, nand_8_out;

  not nand_1 (nand_1_out, S0);  // NAND_Gate
  not nand_2 (nand_2_out, S1);  // NAND_Gate
  not nand_3 (nand_3_out, S1);  // NAND_Gate
  not nand_4 (nand_4_out, S0);  // NAND_Gate
  nand nand_5 (nand_5_out, nand_1_out, nand_2_out, D0);
  nand nand_6 (nand_6_out, nand_3_out, S0, D1);
  nand nand_7 (nand_7_out, nand_4_out, S1, D2);
  nand nand_8 (nand_8_out, S1, S0, D3);
  nand nand_9 (Y, nand_5_out, nand_6_out, nand_7_out, nand_8_out);
endmodule
